# Fritzing sketch DC (saved by Fritzing 1.0.1rc)
breadboards: 1

parts:
  MCU = Arduino Uno (Rev3)
  R1 = Resistor [tolerance=±5% resistance=220 package="0603 [SMD]"]
  LED1 = LED - 5mm [color="Red (633nm)" current=0.030A package="5 mm [THT]"]

nets:
  N1: MCU.5V, R1.Pin_0
  N2: MCU.GND, LED1.cathode
  N3: R1.Pin_1, LED1.anode
