# Fritzing sketch PushButton-Series (saved by Fritzing 1.0.1rc)
breadboards: 1

parts:
  MCU = Arduino Uno (Rev3)
  R1 = Resistor [tolerance=±5% resistance=220 package="0603 [SMD]"]
  LED1 = LED - 5mm [color="Red (633nm)" current=0.030A package="5 mm [THT]"]
  S1 = Pushbutton [package="[THT]"]
  S2 = Pushbutton [package="[THT]"]

nets:
  N1: MCU.GND, S2.Pin_1, S2.Pin_2
  N2: MCU.5V, R1.Pin_0
  N3: R1.Pin_1, LED1.anode
  N4: LED1.cathode, S1.Pin_3, S1.Pin_4
  N5: S1.Pin_1, S1.Pin_2, S2.Pin_3, S2.Pin_4
