# Fritzing sketch ch02 (saved by Fritzing 1.0.1rc)
breadboards: 1

parts:
  LED3 = LED - 5mm [color="Red (633nm)" current=30mA package="5 mm [THT]"]
  LED2 = LED - 5mm [color="Red (633nm)" current=30mA package="5 mm [THT]"]
  LED1 = LED - 5mm [color="Green (555nm)" current=30mA package="5 mm [THT]"]
  MCU = Arduino Uno (Rev3)
  S1 = Pushbutton [package="[THT]"]
  R3 = Resistor [tolerance=±5% resistance=220 package="0603 [SMD]"]
  R2 = Resistor [tolerance=±5% resistance=220 package="0603 [SMD]"]
  R1 = Resistor [tolerance=±5% resistance=220 package="0603 [SMD]"]
  R4 = Resistor [tolerance=±5% resistance=10 package="0603 [SMD]"]

nets:
  N1: LED3.cathode, R3.Pin_1
  N2: LED3.anode, MCU.D5_PWM
  N3: LED2.cathode, R2.Pin_1
  N4: LED2.anode, MCU.D4
  N5: LED1.cathode, R1.Pin_1
  N6: LED1.anode, MCU.D3_PWM
  N7: MCU.D2, S1.Pin_1, S1.Pin_2, R4.Pin_1
  N8: MCU.5V, S1.Pin_3, S1.Pin_4
  N9: MCU.GND, R3.Pin_0, R2.Pin_0, R1.Pin_0, R4.Pin_0
