# Fritzing sketch ch03 (saved by Fritzing 1.0.1rc)
breadboards: 1

parts:
  LED3 = LED - 5mm [color="Red (633nm)" current=30mA package="5 mm [THT]"]
  LED2 = LED - 5mm [color="Red (633nm)" current=30mA package="5 mm [THT]"]
  MCU = Arduino Uno (Rev3)
  R3 = Resistor [tolerance=±5% resistance=220 package="0603 [SMD]"]
  R2 = Resistor [tolerance=±5% resistance=220 package="0603 [SMD]"]
  R1 = Resistor [tolerance=±5% resistance=220 package="0603 [SMD]"]
  T1 = TMP36 Temperature Sensor [package="TO92 [THT]"]
  LED3_2 = LED - 5mm [color="Red (633nm)" current=30mA package="5 mm [THT]"]

nets:
  N1: LED3.cathode, R3.Pin_1
  N2: LED3.anode, MCU.D4
  N3: LED2.cathode, R2.Pin_1
  N4: LED2.anode, MCU.D3_PWM
  N5: MCU.A0, T1.Vout
  N6: MCU.D2, LED3_2.anode
  N7: MCU.5V, T1.+Vs
  GND: MCU.GND, R3.Pin_0, R2.Pin_0, R1.Pin_0, T1.GND
  N8: R1.Pin_1, LED3_2.cathode
