# Fritzing sketch ch04 (saved by Fritzing 1.0.1rc)
breadboards: 1

parts:
  MCU = Arduino Uno (Rev3)
  R3 = Resistor [tolerance=±5% resistance=10 package="0603 [SMD]"]
  R2 = Resistor [tolerance=±5% resistance=10 package="0603 [SMD]"]
  R1 = Resistor [tolerance=±5% resistance=10 package="0603 [SMD]"]
  Q2 = LTR-301 [package=ltr-301]
  Q3 = LTR-301 [package=ltr-301]
  Q1 = LTR-301 [package=ltr-301]
  LED1 = RGB LED (com. cathode, rbg) [color="Red (633nm)" current=0.030A package="5 mm [THT]"]

nets:
  N1: MCU.A0, R1.Pin_1, Q1.E
  N2: MCU.A1, R2.Pin_1, Q2.E
  N3: MCU.A2, R3.Pin_1, Q3.E
  N4: MCU.D9_PWM, LED1.green_anode
  N5: MCU.D10_PWM/SS, LED1.blue_anode
  N6: MCU.D11_PWM/MOSI, LED1.red_anode
  N7: MCU.5V, Q2.C, Q3.C, Q1.C
  N8: MCU.GND, R3.Pin_0, R2.Pin_0, R1.Pin_0, LED1.common_cathode
