# Fritzing sketch ch05 (saved by Fritzing 1.0.1rc)
breadboards: 1

parts:
  MCU = Arduino Uno (Rev3)
  J1 = Basic Servo
  U2 = POT [knob_status=50% power=0.5W package=3362u]
  C1 = Electrolytic Capacitor [capacitance=0.1mF voltage=35V package="0405 [SMD, electrolytic]"]
  C2 = Electrolytic Capacitor [capacitance=0.1mF voltage=35V package="0405 [SMD, electrolytic]"]

nets:
  N1: MCU.A0, U2.S
  N2: MCU.D9_PWM, J1.pulse
  5V: MCU.5V, J1.vcc, U2.A, C1.+, C2.+
  GND: MCU.GND, J1.gnd, U2.E, C1.-, C2.-
