# Fritzing sketch ch06 (saved by Fritzing 1.0.1rc)
breadboards: 1

parts:
  MCU = Arduino Uno (Rev3)
  SG1 = Buzzer 12mm [package=buzzer-12mm-ns]
  Q1 = LTR-301 [package=ltr-301]
  R1 = Resistor [tolerance=±5% resistance=220 package="0402 [SMD]"]

nets:
  N1: MCU.A0, Q1.E, R1.Pin_0
  N2: MCU.D8, SG1.2
  N3: MCU.GND, SG1.1, R1.Pin_1
  N4: MCU.5V, Q1.C
