# Fritzing sketch ch07 (saved by Fritzing 1.0.1rc)
breadboards: 1

parts:
  MCU = Arduino Uno (Rev3)
  SG1 = Buzzer 12mm [package=buzzer-12mm-ns]
  R2 = Resistor [tolerance=±5% resistance=10000 package="0402 [SMD]"]
  R1 = Resistor [tolerance=±5% resistance=220 package="0402 [SMD]"]
  R3 = Resistor [tolerance=±5% resistance=1000000 package="0402 [SMD]"]
  R4 = Resistor [tolerance=±5% resistance=10000 package="0402 [SMD]"]
  S4 = Pushbutton [package="[SMD]"]
  S1 = Pushbutton [package="[SMD]"]
  S2 = Pushbutton [package="[SMD]"]
  S3 = Pushbutton [package="[SMD]"]

nets:
  N1: MCU.A0, R4.Pin_0, S4.Pin_3, S4.Pin_4, S1.Pin_3, S1.Pin_4, S2.Pin_3, S2.Pin_4, S3.Pin_3, S3.Pin_4
  N2: MCU.D8, SG1.2
  N3: MCU.GND, SG1.1, R4.Pin_1
  N4: MCU.5V, R2.Pin_1, R1.Pin_1, R3.Pin_1, S4.Pin_1, S4.Pin_2
  N5: R2.Pin_0, S2.Pin_1, S2.Pin_2
  N6: R1.Pin_0, S1.Pin_1, S1.Pin_2
  N7: R3.Pin_0, S3.Pin_1, S3.Pin_2
