# Fritzing sketch ch09 (saved by Fritzing 1.0.1rc)
breadboards: 1

parts:
  R7 = Resistor [tolerance=±5% resistance=10000 package="0805 [SMD]"]
  S1 = Pushbutton [package="[SMD]"]
  MCU = Arduino Uno (Rev3)
  Q1 = Basic FET N-Channel [package="TO220 [THT]"]
  D1 = Rectifier Diode [part_number=1N4001 package="300 mil [THT]"]
  VCC1 = Battery block 9V
  M1 = DC Motor [voltage_(max)=6V voltage_(min)=3V]

nets:
  N1: R7.Pin_0, MCU.GND, Q1.source, VCC1.-
  N2: R7.Pin_1, S1.Pin_3, S1.Pin_4, MCU.D2
  N3: S1.Pin_1, S1.Pin_2, MCU.5V
  N4: MCU.D9_PWM, Q1.gate
  N5: Q1.drain, D1.anode, M1.pin_1
  N6: D1.cathode, VCC1.+, M1.pin_2
