# Fritzing sketch ch10 (saved by Fritzing 1.0.1rc)
breadboards: 1

parts:
  S1 = Pushbutton [package="[SMD]"]
  MCU = Arduino Uno (Rev3)
  VCC1 = Battery block 9V
  M1 = DC Motor [voltage_(max)=6V voltage_(min)=3V]
  IC1 = L293D [package=THT]
  U1 = POT [knob_status=50% power=0.5W package=3362u]
  S2 = Pushbutton [package="[SMD]"]
  R1 = Resistor [tolerance=±5% power=0.25W resistance=10000 package=THT]
  R2 = Resistor [tolerance=±5% power=0.25W resistance=10000 package=THT]

nets:
  N1: S1.Pin_1, S1.Pin_2, MCU.D4, R1.Pin_0
  N2: S1.Pin_3, S1.Pin_4, MCU.5V, IC1.+V, U1.E, S2.Pin_3, S2.Pin_4
  N3: MCU.A0, U1.S
  N4: MCU.D9_PWM, IC1.Enable_1
  N5: MCU.GND, VCC1.-, IC1.0V, U1.A, R1.Pin_1, R2.Pin_1
  N6: MCU.D2, IC1.In_2
  N7: MCU.D3_PWM, IC1.In_1
  N8: MCU.D5_PWM, S2.Pin_1, S2.Pin_2, R2.Pin_0
  N9: VCC1.+, IC1.+Vmotor
  N10: M1.pin_1, IC1.Out_1_(_Controlled_by_Enable_1_)
  N11: M1.pin_2, IC1.Out_2_(_Controlled_by_Enable_1_)
